# Fritzing sketch superMaquina (saved by Fritzing 0.9.3b)
circuit board: 6.98257cm x 5.45238cm
breadboards: 1

parts:
  LED1 = LED - 5mm [color="Red (633nm)" package="5 mm [THT]"]
  R1 = Resistor [tolerance=±5% resistance=330 package=THT]
  Componente1 = Arduino Uno (Rev3)

nets:
  N1: LED1.cathode, R1.Pin_0
  N2: LED1.anode, Componente1.D13/SCK
  N3: R1.Pin_1, Componente1.GND

// code stored in the sketch: superMaquina.ino
/*
   Efeito sequencial de leds ("super máquina")
   author José de Assis
*/

//a linha abaixo cria uma variável global do tipo inteiro
int valor = 100;

void setup() {
  pinMode(9, OUTPUT);
  pinMode(10, OUTPUT);
  pinMode(11, OUTPUT);
  pinMode(12, OUTPUT);
  pinMode(13, OUTPUT);
}

void loop() {
  for (int i = 9; i < 14; i++) {
    digitalWrite(i, HIGH);
    delay(valor);
    digitalWrite(i, LOW);
  }
  for (int i = 12; i > 9; i--){
    digitalWrite(i, HIGH);
    delay(valor);
    digitalWrite(i, LOW);
  }
}

// code stored in the sketch: Untitled.ino

